# Fritzing sketch Circuit (saved by Fritzing 0.9.3b)
breadboards: 1

parts:
  Raspberry_Pi_1 = Raspberry Pi 3 [part_number=RPI-3-V1.2]
  LED1 = RGB LED (com. cathode, rgb) [package="5 mm [THT]"]
  J1 = Piezo Speaker
  Q2 = MOSFET-NCHANNEL [package=to220v]
  Q3 = MOSFET-NCHANNEL [package=to220v]
  Q4 = MOSFET-NCHANNEL [package=to220v]
  RHT1 = Humidity and Temperature Sensor RHT03

nets:
  3V3: Raspberry_Pi_1.3v3, RHT1.Vcc
  N1: Raspberry_Pi_1.GIPO17, Q2.G
  N2: Raspberry_Pi_1.GIPO22, Raspberry_Pi_1.GND, J1.pin1, Q2.S, Q3.G, Q3.S, Q4.S, RHT1.GND_2
  N3: Raspberry_Pi_1.GIPO6, J1.pin2
  N4: Raspberry_Pi_1.GIPO12, RHT1.Data-signal
  N5: Raspberry_Pi_1.GIPO24, Q4.G
  N6: LED1.red_anode, Q2.D
  N7: LED1.green_anode, Q3.D
  N8: LED1.blue_anode, Q4.D

notes:
  mz80 kabloları
  kırmızı Vcc
  sarı signal
  siyah ground
  bu hat 12 V Gnd ve + olacak

// code stored in the sketch: home sec.ino

